# Fritzing sketch VM167Box (saved by Fritzing 1.0.3b)
circuit board: 12.5159cm x 8.12482cm
perfboards: 1

parts:
  R5 = Resistor [tolerance=±5% power=0.25W resistance=10k package=THT]
  R1 = Resistor [tolerance=±5% power=0.25W resistance=100 package=THT]
  C1 = Electrolytic Capacitor [capacitance=1µF voltage=35V package="100 mil [THT, electrolytic]"]
  Fuse1 = Fuse with Handler [part_number=Htc-15m]
  R6 = Resistor [tolerance=±5% power=0.25W resistance=10k package=THT]
  R4 = Resistor [tolerance=±5% power=0.25W resistance=100 package=THT]
  Q2 = npn-Powertransistor [package="TO220 [THT]"]
  R2 = Resistor [tolerance=±5% power=0.25W resistance=100 package=THT]
  J1 = male pin header, 8 pins [form="♂ (male)"]
  J9 = male pin header, 2 pins [form="♂ (male)"]
  Q1 = npn-Powertransistor [package="TO220 [THT]"]
  R6_2 = Resistor [tolerance=±5% power=0.25W resistance=10k package=THT]
  R8 = Resistor [tolerance=±5% power=0.25W resistance=10k package=THT]
  R3 = Resistor [tolerance=±5% power=0.25W resistance=100 package=THT]
  C2 = Electrolytic Capacitor [capacitance=1µF voltage=35V package="100 mil [THT, electrolytic]"]
  J5 = male pin header, 9 pins [form="♂ (male)"]
  J2 = female pin header, 8 pins [form="♀ (female)"]
  J3 = female pin header, 8 pins [form="♀ (female)"]
  U2 = LM 358 Dual Op-Amp [package="DIP8 [THT]"]
  J4 = screw terminal, 8 pins
  J8 = screw terminal, 9 pins
  J12 = Screw terminal - 2 pins [package=THT]
  VR1 = Potentiometer [mn=5k package="DIP [THT]"]
  J23 = Audio Jack 3.5mm [part_number=3.5mm package="[THT]"]
  J24 = Audio Jack 3.5mm [part_number=3.5mm package="[THT]"]
  J25 = Audio Jack 3.5mm [part_number=3.5mm package="[THT]"]
  J26 = Audio Jack 3.5mm [part_number=3.5mm package="[THT]"]
  VR1_2 = Trimpot-3296 [mn=20k package=3386u]
  Power_plug1 = Power plug
  J6 = female pin header, 9 pins [form="♀ (female)"]
  J7 = female pin header, 9 pins [form="♀ (female)"]
  J10 = female pin header, 2 pins [form="♀ (female)"]
  J11 = female pin header, 2 pins [form="♀ (female)"]
  J22 = female pin header, 2 pins [form="♀ (female)"]
  J14 = female pin header, 2 pins [form="♀ (female)"]
  J15 = female pin header, 2 pins [form="♀ (female)"]
  J21 = female pin header, 2 pins [form="♀ (female)"]
  J19 = female pin header, 2 pins [form="♀ (female)"]
  J18 = female pin header, 2 pins [form="♀ (female)"]
  J17 = female pin header, 2 pins [form="♀ (female)"]
  J16 = female pin header, 2 pins [form="♀ (female)"]
  J13 = female pin header, 2 pins [form="♀ (female)"]
  D2 = Rectifier Diode 500mil [part_number=1N5408 package="500 mil [THT]"]
  D6 = Rectifier Diode 500mil [part_number=1N5408 package="500 mil [THT]"]
  D4 = Rectifier Diode 500mil [part_number=1N5408 package="500 mil [THT]"]
  D8 = Rectifier Diode 500mil [part_number=1N5408 package="500 mil [THT]"]
  D1 = Rectifier Diode 500mil [part_number=1N5408 package="500 mil [THT]"]
  D3 = Rectifier Diode 500mil [part_number=1N5408 package="500 mil [THT]"]
  D5 = Rectifier Diode 500mil [part_number=1N5408 package="500 mil [THT]"]
  D7 = Rectifier Diode 500mil [part_number=1N5408 package="500 mil [THT]"]
  D9 = Rectifier Diode 500mil [part_number=1N5408 package="500 mil [THT]"]
  D10 = Rectifier Diode 500mil [part_number=1N5408 package="500 mil [THT]"]
  RCA2 = RCA [package=pth]
  RCA1 = RCA [package=pth]
  J27 = male pin header, 4 pins [form="♂ (male)"]
  J29 = female pin header, 3 pins [form="♀ (female)"]
  J28 = female pin header, 3 pins [form="♀ (female)"]
  VR2 = Trimpot-3296 [mn=20k package=3386u]

nets:
  N1: R5.Pin_0, C2.+, U2.connector4, J21.pin1, J21.pin2
  N2: R5.Pin_1, J15.pin1, J15.pin2
  N3: R1.Pin_0, J23.Ring_1
  N4: R1.Pin_1, R4.Pin_1, R2.Pin_1, J9.pin1, R3.Pin_1, J12.pin1, VR1.B2, J10.pin1, J11.pin1, D1.cathode, D3.cathode, D5.cathode, D7.cathode
  GND: C1.-, R6.Pin_0, J1.pin8, J9.pin2, R8.Pin_1, C2.-, J5.pin9, J2.pin8, J3.pin8, U2.connector3, J4.pin8, J8.pin9, J12.pin2, VR1.A1, J23.GND, J24.GND, J25.GND, J26.GND, Power_plug1.GND, J6.pin9, J7.pin9, J10.pin2, J11.pin2, D2.anode, D6.anode, D4.anode, D8.anode, D9.anode, D10.anode, RCA2.SHELL, RCA1.SHELL, J27.pin4
  N5: C1.+, R6_2.Pin_0, U2.connector2, J22.pin1, J22.pin2
  N6: Fuse1.Connector1, Power_plug1.VCC
  N7: Fuse1.Connector2, Q2.collector, Q1.collector, U2.connector7
  N8: R6.Pin_1, U2.connector1, VR1_2.WIPER
  N9: R4.Pin_0, J26.Ring_1
  N10: Q2.base, U2.connector6, VR2.CCW
  N11: Q2.emitter, D10.cathode, RCA2.PIN
  N12: R2.Pin_0, J24.Ring_1
  N13: J1.pin1, J2.pin1, J3.pin1, J4.pin1
  N14: J1.pin2, J2.pin2, J3.pin2, J4.pin2
  N15: J1.pin3, J2.pin3, J3.pin3, J4.pin3
  N16: J1.pin4, J2.pin4, J3.pin4, J4.pin4
  N17: J1.pin5, J2.pin5, J3.pin5, J4.pin5
  N18: J1.pin6, J2.pin6, J3.pin6, J4.pin6
  N19: J1.pin7, J2.pin7, J3.pin7, J4.pin7
  N20: Q1.base, U2.connector0, VR1_2.CCW
  N21: Q1.emitter, D9.cathode, RCA1.PIN
  N22: R6_2.Pin_1, J14.pin1, J14.pin2
  N23: R8.Pin_0, U2.connector5, VR2.WIPER
  N24: R3.Pin_0, J25.Ring_1
  N25: J5.pin1, J8.pin1, J6.pin1, J7.pin1
  N26: J5.pin2, J8.pin2, J6.pin2, J7.pin2
  N27: J5.pin3, J8.pin3, J6.pin3, J7.pin3
  N28: J5.pin4, J8.pin4, J6.pin4, J7.pin4
  N29: J5.pin5, J8.pin5, J6.pin5, J7.pin5
  N30: J5.pin6, J8.pin6, J6.pin6, J7.pin6
  N31: J5.pin7, J8.pin7, J6.pin7, J7.pin7
  N32: J5.pin8, J8.pin8, J6.pin8, J7.pin8
  N33: VR1.Wiper, VR1.SW1
  N34: VR1.SW2, J13.pin1, J13.pin2
  N35: J23.Tip_2, J16.pin1
  N36: J23.Tip_1, J16.pin2, D2.cathode, D1.anode
  N37: J24.Tip_2, J17.pin1
  N38: J24.Tip_1, J17.pin2, D4.cathode, D3.anode
  N39: J25.Tip_2, J18.pin1
  N40: J25.Tip_1, J18.pin2, D6.cathode, D5.anode
  N41: J26.Tip_2, J19.pin1
  N42: J26.Tip_1, J19.pin2, D8.cathode, D7.anode
  N43: J27.pin1, J29.pin1, J28.pin1
  N44: J27.pin2, J29.pin2, J28.pin2
  N45: J27.pin3, J29.pin3, J28.pin3

notes:
  VM167Box rev 0
  © Capnode AB 2024

custom parts:
  Potentiometer: Potentiometer with switch
  Audio Jack 3.5mm: Audio Jack Mono/Stereo 3.5mm
  Trimpot-3296: Trimpot 3296 / 25 turn stand
  Power plug: power plug
  Rectifier Diode 500mil: A standard rectifier diode streched to 500mil
